# Fritzing sketch psycho_garbanzo (saved by Fritzing 0.9.6b)
circuit board: 8.46667cm x 5.64444cm

parts:
  LCD1 = 2.8" SPI TFT Module [part_number=MSP2807]
  esp1 = ESP32 DevKitc V4
  Компонент1 = Thumb Joystick
  J2 = female pin header, 2 pins [form="♀ (female)"]
  J3 = female pin header, 2 pins [form="♀ (female)"]
  Bat1 = battery_holder_dual_18650 [part_number=TBH-18650-2A-P]
  M1 = TP4056 Module [part_number=HW-107]
  R1 = Resistor [tolerance=±10% resistance=10k package="0805 [SMD]"]
  J4 = female pin header, 3 pins [form="♀ (female)"]
  J4_2 = rounded female pin header, 4 pins [form="♀ (female rounded)"]  # not connected
  J4_3 = female pin header, 4 pins [form="♀ (female)"]
  J5 = rounded female pin header, 4 pins [form="♀ (female rounded)"]  # not connected
  J6 = female pin header, 4 pins [form="♀ (female)"]
  J7 = female pin header, 3 pins [form="♀ (female)"]
  J8 = rounded female pin header, 4 pins [form="♀ (female rounded)"]
  J9 = female pin header, 4 pins [form="♀ (female)"]  # not connected
  J10 = female pin header, 3 pins [form="♀ (female)"]
  J11 = rounded female pin header, 4 pins [form="♀ (female rounded)"]
  J12 = female pin header, 4 pins [form="♀ (female)"]
  J13 = female pin header, 3 pins [form="♀ (female)"]
  J14 = rounded female pin header, 5 pins [form="♀ (female rounded)"]
  J14_2 = rounded female pin header, 5 pins [form="♀ (female rounded)"]
  J15 = rounded female pin header, 5 pins [form="♀ (female rounded)"]
  S1 = Round Pushbutton
  S2 = Round Pushbutton
  S3 = Round Pushbutton
  S4 = Round Pushbutton
  A1 = NEO-6M GPS Module [part_number=GY-GPS6MV2]
  R2 = Resistor [tolerance=±5% resistance=220 package="1206 [SMD]"]
  Q1 = Basic FET N-Channel [package="D2Pak [SMD]"]
  R3 = Resistor [tolerance=±5% resistance=220 package="0402 [SMD]"]
  S5 = Toggle Switch [package=THT]
  M2 = MT3608 Module
  Компонент2 = PN532 Elechouse RFID NFC Module V3
  IC1 = MCP23017 I2C I/O Expander

nets:
  N1: LCD1.pin1, LCD1.pin8, esp1.3V3
  N2: LCD1.pin2, esp1.GND#18, Компонент1.GND
  N3: LCD1.pin3, esp1.IO15
  N4: LCD1.pin4, esp1.EN
  N5: LCD1.pin5, esp1.IO2
  N6: LCD1.pin6, LCD1.pin13, LCD1.pin16, esp1.IO19, J15.pin2
  N7: LCD1.pin7, LCD1.pin10, LCD1.pin15, esp1.IO18, J14.pin2, J14_2.pin2
  N8: LCD1.pin9, LCD1.pin12, LCD1.pin17, esp1.IO23, J14.pin3, J14_2.pin3
  N9: LCD1.pin11, esp1.IO4
  N10: LCD1.pin18, esp1.IO5, J15.pin3
  N11: esp1.IO16, A1.Tx
  N12: esp1.IO17, A1.Rx
  N13: esp1.IO21, J6.pin2, J11.pin2, Компонент2.SDA
  N14: esp1.RX, J3.pin2
  N15: esp1.TX, J2.pin2
  N16: esp1.IO22, J4.pin2, J8.pin2, Компонент2.SCL, IC1.SCL
  N17: esp1.IO34, Компонент2.RSTO
  N18: esp1.IO32, R1.Pin_0
  N19: esp1.IO33, Компонент1.VERT
  N20: esp1.IO26, Компонент1.HORZ
  N21: esp1.IO27, Компонент1.SEL
  N22: esp1.GND#32, S2.leg1, S3.leg1, S4.leg1
  N23: esp1.IO13, R2.Pin_1, R3.Pin_0
  VCC: esp1.5V, Компонент1.VCC, A1.Vcc, M2.pin3, Компонент2.VCC
  N24: J2.pin1, J4_3.pin1, J10.pin1, J15.pin1
  N25: J3.pin1, J7.pin1, J12.pin1, J14.pin1, J14_2.pin1, IC1.RESET
  N26: Bat1.+#0, Bat1.+#1, S5.COM
  N27: Bat1.+#2, R1.Pin_1
  N28: Bat1.+#3, M1.BAT-, S5.L1
  N29: M1.OUT-#1, M2.pin1
  N30: M1.BAT+, S5.L2
  N31: M1.OUT-#4, M2.pin2
  N32: J4.pin3, IC1.GPB0
  N33: J4_3.pin4, IC1.GPB2
  N34: J6.pin4, IC1.GPB3
  N35: J8.pin3, IC1.GPB4
  N36: J8.pin4, IC1.GPB5
  N37: J11.pin3, IC1.GPB6
  N38: J11.pin4, IC1.GPB7
  N39: J13.pin1, IC1.SDA
  N40: J13.pin2, IC1.GPB1
  N41: J14_2.pin4, IC1.GPA7
  N42: J14_2.pin5, IC1.GPA6
  N43: J15.pin4, IC1.GPA5
  N44: J15.pin5, IC1.GPA4
  N45: S1.leg0, IC1.GPA3
  N46: S2.leg0, IC1.GPA1
  N47: S3.leg0, IC1.GPA2
  N48: S4.leg0, IC1.GPA0
  N49: A1.GND, Q1.drain
  GND: Q1.source, M2.pin4, Компонент2.GND, IC1.VSS
  N50: IC1.A0, IC1.A1

notes:
  Для определения уровня зряда(фиолетовый)
  1)RX TX SERIAL TERMINAL
  2)i2c
  3)i2c
  3)SPI

custom parts:
  2.8" SPI TFT Module: A generic 2.8 inch LCD TFT 320x240 display with touchscreen and SD card slot. Uses the ILI9341 controller, like the Adafruit displays of this size uses.
  ESP32 DevKitc V4: ESP32-DevKitC board with ESP32-WROOM-32 module. ESP32-DevKitC V4 is a small-sized ESP32-based development board produced by Espressif. Most of the pins on the ESP module are broken out to the pin headers on the board. The pins D0, D1, D2, D3, CMD and CLK are used internally for communication between ESP32 and SPI flash memory. They are grouped on both sides near the USB connector. Avoid using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
  battery_holder_dual_18650: TBH-18650-2A-P dual 18650 battery holder.
  TP4056 Module: TP4056 Lithium Battery Charge Management Module Links: TP4056 website
  NEO-6M GPS Module: GY-GPS6MV2 NEO-6M GPS Module Module based on U-blox NEO-6M GPS engine, incorporating regulator for 3.3-5V DC input, MS621FE-compatible rechargeable battery for backup and EEPROM for storing configuration settings. Links: NEO-6 series product information page NEO-6 Datasheet
  MT3608 Module: MT3608 Boost Converter Module Links: Aerosemi MT3608 2A Step Up Converter datasheet
  PN532 Elechouse RFID NFC Module V3: NFC is a popular technology in recent years. We often heard this work while smart phone company such as Samsung or HTC introduces their latest high-end phones. Almost all the high-end phone in the market support NFC. Near field communication (NFC) is a set of standards for smart phones and similar devices to establish radio communication with each other by touching them together or bringing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
  MCP23017 I2C I/O Expander: The MCP23017 uses two i2c pins (these can be shared with other i2c devices), and in exchange gives you 16 general purpose pins. You can set each of 16 pins to be input, output, input with a pullup or open drain. There's even the ability to get an interrupt via an external pin when any of the inputs change so you don't have to keep polling the chip.
